# Fritzing sketch Servo_CdS (saved by Fritzing 0.9.3b)
circuit board: 8.46667cm x 5.64444cm
breadboards: 1

parts:
  부품1 = Arduino Uno (Rev3)
  R2 = Photocell (LDR) [package=THT]
  R3 = Resistor [tolerance=±5% resistance=220 package=THT]
  J1 = Basic Servo

nets:
  N1: 부품1.A0, R2.pin_1, R3.Pin_1
  N2: 부품1.D3_PWM, J1.pulse
  5V: 부품1.5V, R3.Pin_0, J1.vcc
  GND: 부품1.GND, R2.pin_0, J1.gnd
